// Logisim project 8421 to 8421+2.circ as structural Verilog: 1 circuit, main circuit main
module main (
  input  [3:0] \Д8421 ,
  output [3:0] \Д8421___2 
);

  wire not_1_out, not_2_out, not_3_out, not_4_out, not_5_out, or_1_out, or_2_out, or_3_out, or_4_out,
       or_5_out;

  not not_1 (not_1_out, \Д8421 [3]);
  not not_2 (not_2_out, \Д8421 [2]);
  not not_3 (not_3_out, \Д8421 [1]);
  not not_4 (not_4_out, \Д8421 [1]);
  not not_5 (not_5_out, \Д8421 [2]);
  not not_6 (\Д8421___2 [1], \Д8421 [1]);
  or or_1 (or_1_out, \Д8421 [3], \Д8421 [2]);
  or or_2 (or_2_out, \Д8421 [3], \Д8421 [1]);
  and and_1 (\Д8421___2 [3], or_1_out, or_2_out, or_3_out);
  or or_3 (or_3_out, not_1_out, not_2_out, not_3_out);
  or or_4 (or_4_out, not_4_out, not_5_out);
  or or_5 (or_5_out, \Д8421 [1], \Д8421 [2]);
  and and_2 (\Д8421___2 [2], or_4_out, or_5_out);
  // Probe on {\Д8421___2 [3:1], \Д8421 [0]}

  assign \Д8421___2 [0] = \Д8421 [0];
endmodule
