// Logisim project lab_5.circ as structural Verilog: 1 circuit, main circuit main
module main (
  input  in_1
);

  wire and_1_out, and_2_out, not_1_out, t_ff_1_qn, t_ff_2_qn, V_out;
  wire [2:0] t_ff_1_q;

  Clock V (.out(V_out));
  not not_1 (not_1_out, in_1);
  and and_1 (and_1_out, t_ff_1_qn, not_1_out);
  and and_2 (and_2_out, and_1_out, t_ff_2_qn, not_1_out);
  T_Flip_Flop t_ff_1 (.clk(V_out), .T(not_1_out), .Q(t_ff_1_q[0]), .Qn(t_ff_1_qn));  // open: preset, reset, en
  T_Flip_Flop t_ff_2 (.clk(V_out), .T(and_1_out), .Q(t_ff_1_q[1]), .Qn(t_ff_2_qn));  // open: preset, reset, en
  T_Flip_Flop t_ff_3 (.clk(V_out), .T(and_2_out), .Q(t_ff_1_q[2]));  // open: Qn, preset, reset, en
  // Probe on t_ff_1_q
endmodule
